# Fritzing sketch LM317 (saved by Fritzing 0.9.1b)
breadboards: 1

parts:
  U1 = Voltage Regulator [package=to220-adj]
  R1 = Resistor [tolerance=±10% resistance=220 package=THT]
  R2 = Resistor [tolerance=±5% resistance=330 package=THT]
  C2 = Ceramic Capacitor [capacitance=0.1µF package="100 mil [THT, multilayer]"]
  C3 = Electrolytic Capacitor [capacitance=2.2µF package="0605 [SMD, electrolytic]"]
  Part1 = Arduino Uno (Rev3) - ICSP

nets:
  N1: U1.ADJ, R1.Pin_0
  N2: U1.IN, R1.Pin_1, R2.Pin_0, C3.+
  N3: U1.OUT, C2.1, Part1.5V
  N4: R2.Pin_1, C2.0, C3.-, Part1.GND

notes:
  5v Channel
  ~3.3v Channel
  http://www.electronics-lab.com/articles/LM317/
