# Fritzing sketch WebClient (saved by Fritzing 0.9.1b)
breadboards: 1

parts:
  U1 = Voltage Regulator [package=to220-adj]
  R1 = Resistor [tolerance=±10% resistance=220 package=THT]
  R2 = Resistor [tolerance=±5% resistance=330 package=THT]
  C2 = Ceramic Capacitor [capacitance=0.1µF package="100 mil [THT, multilayer]"]
  C3 = Electrolytic Capacitor [capacitance=2.2µF package="0605 [SMD, electrolytic]"]
  Part1 = Arduino Uno (Rev3) - ICSP
  U2 = ESP8266 WiFi Module [part_number=ESP8266]

nets:
  N1: U1.ADJ, R1.Pin_0
  N2: U1.IN, R1.Pin_1, R2.Pin_0, C3.+, U2.VCC, U2.CH_PD
  N3: U1.OUT, C2.1, Part1.5V
  GND: R2.Pin_1, C2.0, C3.-, Part1.GND, Part1.RESET, U2.GND
  N4: Part1.D0/RX, U2.RXD
  N5: Part1.D1/TX, U2.TXD

notes:
  5v Channel
  ~3.3v Channel
  http://www.electronics-lab.com/articles/LM317/
  Note: Connecting the Arduino TX line to the ESP RX line without level shifting could be a problem.s

custom parts:
  ESP8266 WiFi Module: Generic WiFi Module based on the ESP8266 with onboard PCB antenna and UART communications
